// Logisim project project0.circ as structural Verilog: 10 circuits, main circuit bardeen
module bardeen (
  input  A,
  input  R,
  input  D,
  output D_2
);

  wire and_1_out, and_2_out, and_3_out, nand_1_out, not_1_out, not_2_out, not_3_out, or_1_out, or_2_out,
       xor_1_out;

  not not_1 (not_1_out, D);
  or or_1 (or_1_out, A, not_1_out);
  nand nand_1 (nand_1_out, R, D);
  and and_1 (and_1_out, A, D);
  and and_2 (and_2_out, or_1_out, nand_1_out);
  not not_2 (not_2_out, A);
  or or_2 (or_2_out, and_1_out, D);
  xor xor_1 (xor_1_out, R, not_2_out);
  not not_3 (not_3_out, xor_1_out);
  and and_3 (and_3_out, not_2_out, R, or_2_out);
  or or_3 (D_2, and_2_out, not_3_out, and_3_out);
endmodule

module shockley (
  input  A,
  input  R,
  input  D,
  output B
);

  wire and_1_out, and_2_out, not_1_out, not_2_out, not_3_out;

  not not_1 (not_1_out, R);
  not not_2 (not_2_out, A);
  not not_3 (not_3_out, D);
  and and_1 (and_1_out, A, not_1_out);
  and and_2 (and_2_out, not_2_out, R);
  or or_1 (B, and_1_out, and_2_out, not_3_out);
endmodule

module onehot (
  input  A,
  input  B,
  input  C,
  output H
);

  wire and_1_out, and_2_out, and_3_out, not_1_out, not_2_out, not_3_out, not_4_out, not_5_out, not_6_out;

  not not_1 (not_1_out, B);
  not not_2 (not_2_out, C);
  not not_3 (not_3_out, A);
  not not_4 (not_4_out, C);
  not not_5 (not_5_out, A);
  not not_6 (not_6_out, B);
  and and_1 (and_1_out, A, not_1_out, not_2_out);
  and and_2 (and_2_out, not_3_out, B, not_4_out);
  and and_3 (and_3_out, not_5_out, not_6_out, C);
  or or_1 (H, and_1_out, and_2_out, and_3_out);
endmodule

module parity (
  input  X,
  input  Y,
  input  Z,
  output P
);

  wire and_1_out, and_2_out, and_3_out, not_1_out, not_2_out, not_3_out;

  not not_1 (not_1_out, X);
  not not_2 (not_2_out, Y);
  not not_3 (not_3_out, Z);
  and and_1 (and_1_out, not_1_out, Y, Z);
  and and_2 (and_2_out, X, not_2_out, Z);
  and and_3 (and_3_out, X, Y, not_3_out);
  or or_1 (P, and_1_out, and_2_out, and_3_out);
endmodule

module election (
  input  A,
  input  B,
  input  C,
  output Y,
  output N
);

  wire and_1_out, and_2_out, and_3_out;

  and and_1 (and_1_out, B, C);
  and and_2 (and_2_out, A, C);
  and and_3 (and_3_out, A, B);
  or or_1 (Y, and_1_out, and_2_out, and_3_out);
  nor nor_1 (N, and_1_out, and_2_out, and_3_out);
endmodule

module railroad (
  input  X,
  input  S,
  input  Y,
  output V
);

  wire and_1_out, and_2_out, not_1_out;

  not not_1 (not_1_out, S);
  and and_1 (and_1_out, X, not_1_out);
  and and_2 (and_2_out, S, Y);
  or or_1 (V, and_1_out, and_2_out);
endmodule

module decoder0 (
  input  [2:0] S,
  output A,
  output B,
  output C,
  output D
);

  wire not_1_out, not_2_out, not_3_out, not_4_out;

  not not_1 (not_1_out, S[1]);
  not not_2 (not_2_out, S[0]);
  not not_3 (not_3_out, S[1]);
  not not_4 (not_4_out, S[0]);
  and and_1 (A, S[2], not_1_out, not_2_out);
  and and_2 (B, S[2], not_3_out, S[0]);
  and and_3 (C, S[2], S[1], not_4_out);
  and and_4 (D, S[2], S[1], S[0]);
endmodule

module counter (
  input  [2:0] V,
  output [3:0] C
);

  wire not_1_out, not_2_out, not_3_out;

  not not_1 (not_1_out, V[0]);
  not not_2 (not_2_out, V[1]);
  and and_1 (C[0], not_1_out, not_2_out, not_3_out);
  not not_3 (not_3_out, V[2]);
  and and_2 (C[1], V[0], V[1], V[2]);
  parity parity_1 (.X(V[0]), .Y(V[1]), .Z(V[2]), .P(C[2]));
  onehot onehot_1 (.A(V[0]), .B(V[1]), .C(V[2]), .H(C[3]));
endmodule

module decoder1 (
  input  [1:0] N,
  output A,
  output B,
  output C,
  output D
);

  wire not_1_out, not_2_out, not_3_out, not_4_out;

  not not_1 (not_1_out, N[0]);
  not not_2 (not_2_out, N[1]);
  not not_3 (not_3_out, N[1]);
  not not_4 (not_4_out, N[0]);
  and and_1 (A, not_1_out, not_2_out);
  and and_2 (B, N[0], not_3_out);
  and and_3 (C, not_4_out, N[1]);
  and and_4 (D, N[0], N[1]);
endmodule

module display (
  input  [1:0] V,
  input  E
);

  wire decoder1_1_a, decoder1_1_b, decoder1_1_c, decoder1_1_d, or_1_out, or_2_out, or_3_out, or_4_out,
       or_5_out;
  wire [2:0] and_4_out, and_6_out;
  wire [4:0] and_3_out;

  or or_1 (or_1_out, decoder1_1_b, decoder1_1_d);
  and and_1 (and_3_out[4], or_1_out, E);
  or or_2 (or_2_out, decoder1_1_d, decoder1_1_a);
  and and_2 (and_6_out[2], or_2_out, E);
  decoder1 decoder1_1 (.N(V), .A(decoder1_1_a), .B(decoder1_1_b), .C(decoder1_1_c), .D(decoder1_1_d));
  or or_3 (or_3_out, decoder1_1_d, decoder1_1_b, decoder1_1_a);
  and and_3 (and_3_out[0], E, or_3_out);
  or or_4 (or_4_out, decoder1_1_c, decoder1_1_d, decoder1_1_b);
  and and_4 (and_4_out[0], E, or_4_out);
  or or_5 (or_5_out, decoder1_1_b, decoder1_1_a);
  and and_5 (and_4_out[2], E, or_5_out);
  DotMatrix #(.matrixcols(4), .matrixrows(5)) dotmatrix_1 (
    .col0({and_3_out[4], {3{E}}, and_3_out[0]}), .col1({E, 1'b0, and_4_out[2], 1'b0, and_4_out[0]}),
    .col2({E, 1'b0, and_4_out[2], 1'b0, and_4_out[0]}), .col3({1'b0, E, and_6_out[2], E, and_6_out[0]}));
  and and_6 (and_6_out[0], E, decoder1_1_a);
endmodule
