// Logisim project sequential-alt.circ as structural Verilog: 16 circuits, main circuit prng
module prng (
  input  [15:0] seed,
  input  reseed,
  input  update,
  output [15:0] \rand 
);

  wire clock_1_out;
  wire [3:0] multiplier_1_cout, multiplier_1_cout_2, multiplier_1_out, multiplier_1_out_2;
  wire [15:0] multiplexer_1_out, multiplier_1_out_3;

  Multiplexer #(.enable("false"), .select(2), .width(16)) multiplexer_1 (
    .in0(\rand ), .in1(multiplier_1_out_3), .in2(seed), .in3(seed), .out(multiplexer_1_out),
    .sel({reseed, update}));
  Register #(.width(16)) register_1 (.D(multiplexer_1_out), .Q(\rand ), .clk(clock_1_out));  // open: en, clr
  Clock clock_1 (.out(clock_1_out));
  Multiplier #(.width(16)) multiplier_1 (
    .a(\rand ), .b(16'h2), .out({multiplier_1_out_3[7:0], multiplier_1_out_2, multiplier_1_out}),
    .cout({multiplier_1_cout_2, multiplier_1_cout, multiplier_1_out_3[15:8]}));  // open: cin
endmodule

module primefinder (
  input  [31:0] StartingNumber,
  output [31:0] PrimeNumber,
  output done,
  output [31:0] C,
  output [31:0] i
);

  wire clo, not_1_out, not_2_out;
  wire [31:0] adder_1_out, adder_2_out, remainder;

  Clock clock_1 (.out(clo));
  Comparator #(.width(32)) comparator_1 (.a(StartingNumber), .b(i), .eq(done));  // open: gt, lt
  Divider #(.width(32)) divider_1 (.a(StartingNumber), .b(i), .rem(remainder));  // open: out, upper
  not not_1 (not_1_out, done);
  Register #(.width(32)) register_1 (.D(adder_1_out), .en(not_1_out), .Q(i), .clk(clo));  // open: clr
  LED u_Done (.in(done));
  Adder #(.width(32)) adder_1 (.a(i), .b(32'h1), .out(adder_1_out));  // open: cin, cout
  not not_2 (not_2_out, done);
  Register #(.width(32)) register_2 (.D(adder_2_out), .en(not_2_out), .Q(i), .clk(clo));  // open: clr
  Adder #(.width(32)) adder_2 (.a(i), .b(32'h1), .out(adder_2_out));  // open: cin, cout

  assign C = StartingNumber;

  // Other names for the same wires on the sheet: candidate[31:0] = StartingNumber; equals = done
endmodule

module manual_calc (
  input  [31:0] USERINPUT,
  input  [1:0] r,
  input  [1:0] p,
  input  [1:0] q,
  input  [2:0] op
);

  wire and_1_out, calc_cmp_1_neg, calc_cmp_1_pos, calc_cmp_1_zero, clock_1_out, decoder_1_out0,
       decoder_1_out1, decoder_1_out2, decoder_1_out3;
  wire [31:0] A_q, B_q, C_q, calc_alu_1_r, D_q, multiplexer_1_out, multiplexer_2_out, multiplexer_3_out;

  Decoder #(.enable("false"), .select(2)) decoder_1 (
    .out0(decoder_1_out0), .out1(decoder_1_out1), .out2(decoder_1_out2), .out3(decoder_1_out3), .sel(r));
  Register #(.width(32)) A (.D(multiplexer_3_out), .en(decoder_1_out0), .Q(A_q), .clk(clock_1_out));  // open: clr
  Register #(.width(32)) B (.D(multiplexer_3_out), .en(decoder_1_out1), .Q(B_q), .clk(clock_1_out));  // open: clr
  Register #(.width(32)) C (.D(multiplexer_3_out), .en(decoder_1_out2), .Q(C_q), .clk(clock_1_out));  // open: clr
  Register #(.width(32)) D (.D(multiplexer_3_out), .en(decoder_1_out3), .Q(D_q), .clk(clock_1_out));  // open: clr
  Clock clock_1 (.out(clock_1_out));
  Multiplexer #(.enable("false"), .select(2), .width(32)) multiplexer_1 (
    .in0(A_q), .in1(B_q), .in2(C_q), .in3(D_q), .out(multiplexer_1_out), .sel(p));
  Multiplexer #(.enable("false"), .select(2), .width(32)) multiplexer_2 (
    .in0(A_q), .in1(B_q), .in2(C_q), .in3(D_q), .out(multiplexer_2_out), .sel(q));
  calc_alu calc_alu_1 (.R(calc_alu_1_r), .P(multiplexer_1_out), .Q(multiplexer_2_out), .FN(op));
  and and_1 (and_1_out, op[0], op[1], op[2]);
  Multiplexer #(.enable("false"), .width(32)) multiplexer_3 (
    .in0(calc_alu_1_r), .in1(USERINPUT), .out(multiplexer_3_out), .sel(and_1_out));
  // Probe on calc_cmp_1_neg
  calc_cmp calc_cmp_1 (.pos(calc_cmp_1_pos), .neg(calc_cmp_1_neg), .zero(calc_cmp_1_zero), .V(multiplexer_3_out));
  // Probe on calc_cmp_1_zero
  // Probe on calc_cmp_1_pos

  // Other names for the same wires on the sheet: tunnel[1:0] = p

  // Notes on the sheet:
  //   This circuit is for practice, where YOU act as the state machine to control the above datapath.
  //   Set the r, p, q, op inputs, click the clock, and see what happens. Learn to control the datapath
  //   to perform a sequence of actions. Your state machine's behavior ultimately must rely only
  //   on the L, Z, and G inputs at right, without actually looking at any of the registers. So make
  //   sure you understand how L, Z, and G can be used to learn something about the register values.
endmodule

module calc_alu (
  input  [31:0] P,
  input  [31:0] Q,
  input  [2:0] FN,
  output [31:0] R
);

  wire [31:0] adder_1_out, divider_1_out, divider_1_rem, multiplier_1_out, subtractor_1_out;

  Adder #(.width(32)) adder_1 (.a(P), .b(Q), .out(adder_1_out));  // open: cin, cout
  Subtractor #(.width(32)) subtractor_1 (.a(P), .b(Q), .out(subtractor_1_out));  // open: bin, bout
  Multiplier #(.width(32)) multiplier_1 (.a(P), .b(Q), .out(multiplier_1_out));  // open: cin, cout
  Divider #(.width(32)) divider_1 (.a(P), .b(Q), .out(divider_1_out), .rem(divider_1_rem));  // open: upper
  Multiplexer #(.enable("false"), .select(3), .width(32)) multiplexer_1 (
    .in0(adder_1_out), .in1(subtractor_1_out), .in2(multiplier_1_out), .in3(divider_1_out),
    .in4(divider_1_rem), .in5({32{1'b0}}), .in6(32'h1), .out(R), .sel(FN));  // open: in7

  // Notes on the sheet:
  //   note: the last mux input
  //   is left disconnected. It
  //   never gets used, because
  //   function 7 (FN=111) takes
  //   a value from user input,
  //   rather than a value
  //   calculated by this ALU.
endmodule

module calc_cmp (
  input  [31:0] V,
  output pos,
  output zero,
  output neg
);

  Comparator #(.width(32)) comparator_1 (.a(V), .b({32{1'b0}}), .gt(pos), .eq(zero), .lt(neg));

  // Notes on the sheet:
  //   This circuit compares the input value, V, against zero. 
  //   The outputs indicate whether V was positive, zero, or negatie.
endmodule

module fib (
  input  [31:0] USERINPUT
);

  wire and_1_out, calc_cmp_1_neg, calc_cmp_1_pos, calc_cmp_1_zero, clock_1_out, clock_2_out, decoder_1_out0,
       decoder_1_out1, decoder_1_out2, decoder_1_out3;
  wire [1:0] fib_fsm_output_table_1_q, fib_fsm_output_table_1_r, tunnel;
  wire [2:0] fib_fsm_output_table_1_op;
  wire [3:0] curstate_q, fib_fsm_transition_table_1_nextstate;
  wire [31:0] A_q, B_q, C_q, calc_alu_1_r, D_q, multiplexer_1_out, multiplexer_2_out, multiplexer_3_out;

  Register #(.width(4)) curstate (
    .D(fib_fsm_transition_table_1_nextstate), .Q(curstate_q), .clk(clock_1_out));  // open: en, clr
  Clock clock_1 (.out(clock_1_out));
  // Probe on curstate_q
  Decoder #(.enable("false"), .select(2)) decoder_1 (
    .out0(decoder_1_out0), .out1(decoder_1_out1), .out2(decoder_1_out2), .out3(decoder_1_out3),
    .sel(fib_fsm_output_table_1_r));
  // Probe on fib_fsm_output_table_1_r
  Register #(.width(32)) A (.D(multiplexer_3_out), .en(decoder_1_out0), .Q(A_q), .clk(clock_2_out));  // open: clr
  Register #(.width(32)) B (.D(multiplexer_3_out), .en(decoder_1_out1), .Q(B_q), .clk(clock_2_out));  // open: clr
  Register #(.width(32)) C (.D(multiplexer_3_out), .en(decoder_1_out2), .Q(C_q), .clk(clock_2_out));  // open: clr
  Register #(.width(32)) D (.D(multiplexer_3_out), .en(decoder_1_out3), .Q(D_q), .clk(clock_2_out));  // open: clr
  Clock clock_2 (.out(clock_2_out));
  fib_fsm_output_table fib_fsm_output_table_1 (
    .curstate(curstate_q), .r(fib_fsm_output_table_1_r), .p(tunnel), .q(fib_fsm_output_table_1_q),
    .op(fib_fsm_output_table_1_op));
  // Probe on tunnel
  Multiplexer #(.enable("false"), .select(2), .width(32)) multiplexer_1 (
    .in0(A_q), .in1(B_q), .in2(C_q), .in3(D_q), .out(multiplexer_1_out), .sel(tunnel));
  Multiplexer #(.enable("false"), .select(2), .width(32)) multiplexer_2 (
    .in0(A_q), .in1(B_q), .in2(C_q), .in3(D_q), .out(multiplexer_2_out), .sel(fib_fsm_output_table_1_q));
  // Probe on fib_fsm_output_table_1_q
  calc_alu calc_alu_1 (.R(calc_alu_1_r), .P(multiplexer_1_out), .Q(multiplexer_2_out), .FN(fib_fsm_output_table_1_op));
  and and_1 (and_1_out, fib_fsm_output_table_1_op[0], fib_fsm_output_table_1_op[1], fib_fsm_output_table_1_op[2]);
  // Probe on fib_fsm_output_table_1_op
  Multiplexer #(.enable("false"), .width(32)) multiplexer_3 (
    .in0(calc_alu_1_r), .in1(USERINPUT), .out(multiplexer_3_out), .sel(and_1_out));
  calc_cmp calc_cmp_1 (.pos(calc_cmp_1_pos), .neg(calc_cmp_1_neg), .zero(calc_cmp_1_zero), .V(multiplexer_3_out));
  fib_fsm_transition_table fib_fsm_transition_table_1 (
    .nextstate(fib_fsm_transition_table_1_nextstate), .curstate(curstate_q), .L(calc_cmp_1_neg),
    .Z(calc_cmp_1_zero), .G(calc_cmp_1_pos));
  // Probe on fib_fsm_transition_table_1_nextstate

  // Notes on the sheet:
  //   This FSM controls the calculator datapath above, causing it to execute the following algorithm, which takes one 
  //   user input, then calculates the fibinacci sequence until it finds a number larger than the user's number. The final 
  //   result is left in register D.
  //   [line 1] do { D = user_input(); } while (D == 0);
  //   [line 2] A = 1;
  //   [line 3] B = 1;
  //   [line 4] while (D - B > 0) { // that is, while D > B...
  //   [line 5]    C = A + B; // calculate next fibonacci number
  //   [line 6]    A = B;
  //   [line 7]    B = C;
  //   [line 8] }
  //   [line 9] D = B; // final result moved into register D
  //   The FSM has twelve states (0 through 11), approximately one state per line of code in the algorithm. Some lines of
  //   code need two states, for example "A = B" is implemented as two steps, "A = 0" then "A = A + B". And there is an extra
  //   "finished" state at the end that does "C=0" in a loop forever, just to stop the algorithm.
  //   state        state      outputs              next state
  //   name         number                          (may depend on L, Z, or G)
  //   [get input]   state 0;  r=3, p=x, q=x, op=7;  if Z=1 then go to state 0, otherwise go to state 1
  //   [init A]      state 1;  r=0, p=x, q=x, op=6;  go to state 2
  //   [init B]      state 2;  r=1, p=x, q=x, op=6;  go to state 3
  //   [compare]     state 3;  r=2, p=3, q=1, op=1;  if G=1 then go to state 4, otherwise go to state 9
  //   [add]         state 4;  r=2, p=0, q=1, op=0;  go to state 5
  //   [erase A]     state 5;  r=0, p=x, q=x, op=5;  go to state 6
  //   [move B to A] state 6;  r=0, p=0, q=1, op=0;  go to state 7
  //   [erase B]     state 7;  r=1, p=x, q=x, op=5;  go to state 8
  //   [move C to B] state 8;  r=1, p=1, q=2, op=0;  go to state 3
  //   [erase D]     state 9;  r=3, p=x, q=x, op=5;  go to state 10
  //   [move C to D] state 10; r=3, p=3, q=1, op=0;  go to state 11
  //   [finished]    state 11: r=2, p=x, q=x, op=6;  go to state 11
endmodule

module fib_fsm_transition_table (
  input  [3:0] curstate,
  input  L,
  input  Z,
  input  G,
  output [3:0] nextstate
);

  wire and_1_out, and_2_out, and_3_out, and_4_out, and_5_out, and_6_out, and_7_out, and_8_out, and_9_out,
       and_10_out, and_11_out, and_12_out, and_13_out, and_14_out, and_15_out;

  and and_1 (and_1_out, curstate[1], curstate[0], ~G);  // AND_Gate
  and and_2 (and_2_out, curstate[2], curstate[1], curstate[0]);
  and and_3 (and_3_out, curstate[3], curstate[0]);
  and and_4 (and_4_out, curstate[3], curstate[1]);
  and and_5 (and_5_out, ~curstate[3], ~curstate[2], curstate[1], curstate[0], G);  // AND_Gate
  and and_6 (and_6_out, curstate[2], ~curstate[1]);  // AND_Gate
  and and_7 (and_7_out, curstate[2], ~curstate[0]);  // AND_Gate
  and and_8 (and_8_out, ~curstate[1], curstate[0]);  // AND_Gate
  and and_9 (and_9_out, curstate[1], ~curstate[0]);  // AND_Gate
  and and_10 (and_10_out, ~curstate[0], ~Z);  // AND_Gate
  and and_11 (and_11_out, ~curstate[2], curstate[1], ~G);  // AND_Gate
  and and_12 (and_12_out, curstate[1], ~curstate[0]);  // AND_Gate
  and and_13 (and_13_out, curstate[2], ~curstate[0]);  // AND_Gate
  and and_14 (and_14_out, curstate[3], ~curstate[0]);  // AND_Gate
  and and_15 (and_15_out, curstate[3], ~curstate[2], curstate[1]);  // AND_Gate
  or or_1 (nextstate[3], and_1_out, and_2_out, and_3_out, and_4_out);
  or or_2 (nextstate[2], and_5_out, and_6_out, and_7_out);
  or or_3 (nextstate[1], and_8_out, and_9_out, curstate[3]);
  or or_4 (nextstate[0], and_10_out, and_11_out, and_12_out, and_13_out, and_14_out, and_15_out);
endmodule

module fib_fsm_output_table (
  input  [3:0] curstate,
  output [1:0] r,
  output [1:0] p,
  output [1:0] q,
  output [2:0] op
);

  wire and_1_out, and_2_out, and_3_out, and_4_out, and_5_out, and_6_out, and_7_out, and_8_out, and_11_out,
       and_12_out, and_13_out, and_14_out, and_15_out, and_16_out, and_17_out, and_18_out, and_19_out,
       and_20_out;

  and and_1 (and_1_out, ~curstate[3], ~curstate[1], ~curstate[0]);  // AND_Gate
  and and_2 (and_2_out, ~curstate[2], curstate[1], curstate[0]);  // AND_Gate
  and and_3 (and_3_out, curstate[3], curstate[0]);
  and and_4 (and_4_out, curstate[3], curstate[1]);
  and and_5 (and_5_out, ~curstate[2], ~curstate[0]);  // AND_Gate
  and and_6 (and_6_out, curstate[2], curstate[1], curstate[0]);
  and and_7 (and_7_out, curstate[3], ~curstate[1]);  // AND_Gate
  and and_8 (and_8_out, curstate[3], ~curstate[0]);  // AND_Gate
  and and_9 (p[1], ~curstate[2], curstate[1]);  // AND_Gate
  not not_1 (p[0], curstate[2]);
  and and_10 (q[1], ~curstate[2], ~curstate[1]);  // AND_Gate
  or or_1 (q[0], ~curstate[3], curstate[1]);  // OR_Gate
  and and_11 (and_11_out, ~curstate[3], ~curstate[2], ~curstate[0]);  // AND_Gate
  and and_12 (and_12_out, ~curstate[1], curstate[0]);  // AND_Gate
  and and_13 (and_13_out, curstate[2], curstate[0]);
  and and_14 (and_14_out, curstate[3], curstate[0]);
  and and_15 (and_15_out, ~curstate[3], ~curstate[2], ~curstate[1]);  // AND_Gate
  and and_16 (and_16_out, ~curstate[3], ~curstate[2], ~curstate[0]);  // AND_Gate
  and and_17 (and_17_out, ~curstate[3], ~curstate[2], ~curstate[1], ~curstate[0]);  // AND_Gate
  and and_18 (and_18_out, curstate[1], curstate[0]);
  and and_19 (and_19_out, curstate[2], curstate[0]);
  and and_20 (and_20_out, curstate[3], curstate[0]);
  or or_2 (r[1], and_1_out, and_2_out, and_3_out, and_4_out);
  or or_3 (r[0], and_5_out, and_6_out, and_7_out, and_8_out);
  or or_4 (op[2], and_11_out, and_12_out, and_13_out, and_14_out);
  or or_5 (op[1], and_15_out, and_16_out);
  or or_6 (op[0], and_17_out, and_18_out, and_19_out, and_20_out);
endmodule

module hailstone (
  input  [31:0] USERINPUT
);

  wire and_1_out, calc_cmp_1_neg, calc_cmp_1_zero, decoder_1_out0, decoder_1_out1, decoder_1_out2,
       decoder_1_out3, rockfella;
  wire [1:0] hailstone_output_table_1_q, hailstone_output_table_1_r, p;
  wire [2:0] hailstone_output_table_1_op;
  wire [3:0] hailstone_transition_table_1_next, register_1_q;
  wire [31:0] A_q, B_q, C_q, calc_alu_1_r, D_q, multiplexer_1_out, multiplexer_2_out, multiplexer_3_out;

  Clock clock_1 (.out(rockfella));
  Register #(.width(4)) register_1 (
    .D(hailstone_transition_table_1_next), .Q(register_1_q), .clk(rockfella));  // open: en, clr
  Decoder #(.enable("false"), .select(2)) decoder_1 (
    .out0(decoder_1_out0), .out1(decoder_1_out1), .out2(decoder_1_out2), .out3(decoder_1_out3),
    .sel(hailstone_output_table_1_r));
  Register #(.width(32)) A (.D(multiplexer_3_out), .en(decoder_1_out0), .Q(A_q), .clk(rockfella));  // open: clr
  Register #(.width(32)) B (.D(multiplexer_3_out), .en(decoder_1_out1), .Q(B_q), .clk(rockfella));  // open: clr
  Register #(.width(32)) C (.D(multiplexer_3_out), .en(decoder_1_out2), .Q(C_q), .clk(rockfella));  // open: clr
  Register #(.width(32)) D (.D(multiplexer_3_out), .en(decoder_1_out3), .Q(D_q), .clk(rockfella));  // open: clr
  hailstone_output_table hailstone_output_table_1 (
    .curr(register_1_q), .r(hailstone_output_table_1_r), .p(p), .q(hailstone_output_table_1_q),
    .op(hailstone_output_table_1_op));
  Multiplexer #(.enable("false"), .select(2), .width(32)) multiplexer_1 (
    .in0(A_q), .in1(B_q), .in2(C_q), .in3(D_q), .out(multiplexer_1_out), .sel(p));
  Multiplexer #(.enable("false"), .select(2), .width(32)) multiplexer_2 (
    .in0(A_q), .in1(B_q), .in2(C_q), .in3(D_q), .out(multiplexer_2_out), .sel(hailstone_output_table_1_q));
  calc_alu calc_alu_1 (
    .R(calc_alu_1_r), .P(multiplexer_1_out), .Q(multiplexer_2_out), .FN(hailstone_output_table_1_op));
  and and_1 (and_1_out, hailstone_output_table_1_op[0], hailstone_output_table_1_op[1], hailstone_output_table_1_op[2]);
  Multiplexer #(.enable("false"), .width(32)) multiplexer_3 (
    .in0(calc_alu_1_r), .in1(USERINPUT), .out(multiplexer_3_out), .sel(and_1_out));
  calc_cmp calc_cmp_1 (.neg(calc_cmp_1_neg), .zero(calc_cmp_1_zero), .V(multiplexer_3_out));  // open: pos
  hailstone_transition_table hailstone_transition_table_1 (
    .Curr(register_1_q), .Z(calc_cmp_1_zero), .L(calc_cmp_1_neg), .Next(hailstone_transition_table_1_next));

  // Notes on the sheet:
  //   r
  //   r
  //   p
  //   Your state machine outputs should
  //   be connected here.
  //   q
  //   Your state machine goes here
  //   op
  //   L
  //   Z
  //   These are the
  //   inputs to your state machine
endmodule

module newton (
  input  [31:0] USERINPUT
);

  wire and_1_out, calc_cmp_1_neg, calc_cmp_1_zero, decoder_1_out0, decoder_1_out1, decoder_1_out2,
       decoder_1_out3, funny;
  wire [1:0] newton_output_table_1_q, newton_output_table_1_r, p;
  wire [2:0] newton_output_table_1_op;
  wire [3:0] newton_transition_table_1_next, register_1_q;
  wire [31:0] A_q, B_q, C_q, calc_alu_1_r, D_q, multiplexer_1_out, multiplexer_2_out, multiplexer_3_out;

  Clock clock_1 (.out(funny));
  Register #(.width(4)) register_1 (
    .D(newton_transition_table_1_next), .Q(register_1_q), .clk(funny));  // open: en, clr
  Decoder #(.enable("false"), .select(2)) decoder_1 (
    .out0(decoder_1_out0), .out1(decoder_1_out1), .out2(decoder_1_out2), .out3(decoder_1_out3),
    .sel(newton_output_table_1_r));
  Register #(.width(32)) A (.D(multiplexer_3_out), .en(decoder_1_out0), .Q(A_q), .clk(funny));  // open: clr
  Register #(.width(32)) B (.D(multiplexer_3_out), .en(decoder_1_out1), .Q(B_q), .clk(funny));  // open: clr
  Register #(.width(32)) C (.D(multiplexer_3_out), .en(decoder_1_out2), .Q(C_q), .clk(funny));  // open: clr
  Register #(.width(32)) D (.D(multiplexer_3_out), .en(decoder_1_out3), .Q(D_q), .clk(funny));  // open: clr
  newton_output_table newton_output_table_1 (
    .Curr(register_1_q), .r(newton_output_table_1_r), .p(p), .q(newton_output_table_1_q),
    .op(newton_output_table_1_op));
  Multiplexer #(.enable("false"), .select(2), .width(32)) multiplexer_1 (
    .in0(A_q), .in1(B_q), .in2(C_q), .in3(D_q), .out(multiplexer_1_out), .sel(p));
  Multiplexer #(.enable("false"), .select(2), .width(32)) multiplexer_2 (
    .in0(A_q), .in1(B_q), .in2(C_q), .in3(D_q), .out(multiplexer_2_out), .sel(newton_output_table_1_q));
  calc_alu calc_alu_1 (.R(calc_alu_1_r), .P(multiplexer_1_out), .Q(multiplexer_2_out), .FN(newton_output_table_1_op));
  and and_1 (and_1_out, newton_output_table_1_op[0], newton_output_table_1_op[1], newton_output_table_1_op[2]);
  Multiplexer #(.enable("false"), .width(32)) multiplexer_3 (
    .in0(calc_alu_1_r), .in1(USERINPUT), .out(multiplexer_3_out), .sel(and_1_out));
  calc_cmp calc_cmp_1 (.neg(calc_cmp_1_neg), .zero(calc_cmp_1_zero), .V(multiplexer_3_out));  // open: pos
  newton_transition_table newton_transition_table_1 (
    .Curr(register_1_q), .Z(calc_cmp_1_zero), .L(calc_cmp_1_neg), .Next(newton_transition_table_1_next));

  // Notes on the sheet:
  //   r
  //   p
  //   Your state machine outputs should
  //   be connected here.
  //   q
  //   Your state machine goes here
  //   op
  //   L
  //   Z
  //   These are the
  //   inputs to your state machine
endmodule

module hailstone_output_table (
  input  [3:0] curr,
  output [1:0] r,
  output [1:0] p,
  output [1:0] q,
  output [2:0] op
);

  wire and_1_out, and_2_out, and_3_out, and_4_out, and_5_out, and_6_out, and_7_out, and_9_out, and_10_out,
       and_11_out, and_12_out, and_13_out, and_14_out, and_15_out, and_16_out, and_17_out, and_18_out,
       and_19_out, and_20_out, and_21_out, and_22_out, and_23_out;

  and and_1 (and_1_out, ~curr[2], curr[1], curr[0]);  // AND_Gate
  and and_2 (and_2_out, ~curr[3], curr[2], ~curr[1]);  // AND_Gate
  and and_3 (and_3_out, curr[3], ~curr[2], curr[0]);  // AND_Gate
  and and_4 (and_4_out, curr[3], curr[1]);
  and and_5 (and_5_out, ~curr[3], ~curr[1], curr[0]);  // AND_Gate
  and and_6 (and_6_out, ~curr[2], curr[1]);  // AND_Gate
  and and_7 (and_7_out, curr[3], curr[1]);
  and and_8 (p[1], ~curr[3], curr[2], ~curr[0]);  // AND_Gate
  and and_9 (and_9_out, ~curr[3], ~curr[1]);  // AND_Gate
  and and_10 (and_10_out, ~curr[3], ~curr[0]);  // AND_Gate
  and and_11 (and_11_out, ~curr[3], curr[2], curr[0]);  // AND_Gate
  and and_12 (and_12_out, curr[3], curr[1]);
  and and_13 (and_13_out, ~curr[3], ~curr[2]);  // AND_Gate
  and and_14 (and_14_out, curr[3], ~curr[1]);  // AND_Gate
  and and_15 (and_15_out, ~curr[3], ~curr[1], ~curr[0]);  // AND_Gate
  and and_16 (and_16_out, ~curr[3], ~curr[2], curr[0]);  // AND_Gate
  and and_17 (and_17_out, ~curr[2], ~curr[1], curr[0]);  // AND_Gate
  and and_18 (and_18_out, ~curr[2], ~curr[1]);  // AND_Gate
  and and_19 (and_19_out, ~curr[3], curr[2], ~curr[0]);  // AND_Gate
  and and_20 (and_20_out, curr[3], ~curr[1]);  // AND_Gate
  and and_21 (and_21_out, ~curr[2], ~curr[1], ~curr[0]);  // AND_Gate
  and and_22 (and_22_out, curr[3], curr[1]);
  and and_23 (and_23_out, curr[3], curr[2]);
  or or_1 (r[1], and_1_out, and_2_out, and_3_out, and_4_out);
  or or_2 (r[0], and_5_out, and_6_out, and_7_out);
  or or_3 (p[0], and_9_out, and_10_out);
  or or_4 (q[1], and_11_out, and_12_out);
  or or_5 (q[0], and_13_out, and_14_out);
  or or_6 (op[2], and_15_out, and_16_out, and_17_out);
  or or_7 (op[1], and_18_out, and_19_out, and_20_out);
  or or_8 (op[0], and_21_out, and_22_out, and_23_out);
endmodule

module hailstone_transition_table (
  input  [3:0] Curr,
  input  Z,
  input  L,
  output [3:0] Next
);

  wire and_1_out, and_2_out, and_3_out, and_4_out, and_5_out, and_6_out, and_7_out, and_8_out, and_9_out,
       and_10_out, and_11_out, and_12_out, and_13_out;

  and and_1 (and_1_out, ~Curr[2], Curr[1], Curr[0], Z);  // AND_Gate
  or or_1 (Next[3], and_1_out, Curr[3]);
  and and_2 (and_2_out, ~Curr[3], ~Curr[2], Curr[1], Curr[0], ~Z);  // AND_Gate
  and and_3 (and_3_out, ~Curr[3], Curr[2], ~Curr[0]);  // AND_Gate
  or or_2 (Next[2], and_2_out, and_3_out, and_4_out);
  and and_4 (and_4_out, Curr[2], ~Curr[1]);  // AND_Gate
  and and_5 (and_5_out, ~Curr[1], Curr[0]);  // AND_Gate
  and and_6 (and_6_out, Curr[1], ~Curr[0]);  // AND_Gate
  and and_7 (and_7_out, Curr[2], Curr[0]);
  and and_8 (and_8_out, Curr[3], Curr[1]);
  and and_9 (and_9_out, ~Curr[1], ~Curr[0], ~Z, ~L);  // AND_Gate
  and and_10 (and_10_out, ~Curr[3], Curr[1], ~Curr[0]);  // AND_Gate
  and and_11 (and_11_out, Curr[2], ~Curr[1], ~Curr[0]);  // AND_Gate
  and and_12 (and_12_out, ~Curr[3], Curr[2], Curr[1]);  // AND_Gate
  and and_13 (and_13_out, Curr[3], ~Curr[1], ~Curr[0]);  // AND_Gate
  or or_3 (Next[1], and_5_out, and_6_out, and_7_out, and_8_out);
  or or_4 (Next[0], and_9_out, and_10_out, and_11_out, and_12_out, and_13_out);
endmodule

module newton_output_table (
  input  [3:0] Curr,
  output [1:0] r,
  output [1:0] p,
  output [1:0] q,
  output [2:0] op
);

  wire and_1_out, and_2_out, and_3_out, and_4_out, and_5_out, and_6_out, and_7_out, and_8_out, and_9_out,
       and_10_out, and_11_out, and_12_out, and_13_out, and_14_out, and_15_out, and_16_out, and_17_out;

  and and_1 (and_1_out, Curr[1], Curr[0]);
  and and_2 (and_2_out, Curr[2], ~Curr[1]);  // AND_Gate
  and and_3 (and_3_out, ~Curr[1], Curr[0]);  // AND_Gate
  and and_4 (and_4_out, Curr[1], ~Curr[0]);  // AND_Gate
  and and_5 (and_5_out, ~Curr[3], ~Curr[1], Curr[0]);  // AND_Gate
  and and_6 (and_6_out, ~Curr[3], Curr[2], Curr[1]);  // AND_Gate
  not not_1 (p[0], Curr[3]);
  and and_7 (and_7_out, ~Curr[2], Curr[0]);  // AND_Gate
  and and_8 (and_8_out, Curr[2], Curr[1]);
  and and_9 (and_9_out, ~Curr[2], ~Curr[0]);  // AND_Gate
  and and_10 (and_10_out, ~Curr[1], Curr[0]);  // AND_Gate
  and and_11 (and_11_out, ~Curr[3], ~Curr[2], ~Curr[1]);  // AND_Gate
  and and_12 (and_12_out, ~Curr[3], Curr[2], Curr[1], Curr[0]);  // AND_Gate
  and and_13 (and_13_out, ~Curr[3], ~Curr[2], ~Curr[1]);  // AND_Gate
  and and_14 (and_14_out, ~Curr[3], Curr[2], ~Curr[0]);  // AND_Gate
  and and_15 (and_15_out, ~Curr[3], Curr[2], Curr[1]);  // AND_Gate
  and and_16 (and_16_out, ~Curr[1], ~Curr[0]);  // AND_Gate
  and and_17 (and_17_out, Curr[2], Curr[1]);
  or or_1 (r[1], and_1_out, and_2_out, Curr[3]);
  or or_2 (r[0], and_3_out, and_4_out, Curr[2], Curr[3]);
  or or_3 (p[1], and_5_out, and_6_out);
  or or_4 (q[1], and_7_out, and_8_out, Curr[3]);
  or or_5 (q[0], and_9_out, and_10_out, Curr[3]);
  or or_6 (op[2], and_11_out, and_12_out);
  or or_7 (op[1], and_13_out, and_14_out, and_15_out);
  or or_8 (op[0], and_16_out, and_17_out, Curr[3]);
endmodule

module newton_transition_table (
  input  [3:0] Curr,
  input  Z,
  input  L,
  output [3:0] Next
);

  wire and_2_out, and_3_out, and_4_out, and_5_out, and_6_out, and_7_out, and_8_out, and_9_out, and_10_out,
       and_11_out;

  and and_1 (Next[3], ~Curr[3], Curr[2], Curr[1], Curr[0]);  // AND_Gate
  and and_2 (and_2_out, ~Curr[3], ~Curr[2], Curr[1], Curr[0]);  // AND_Gate
  and and_3 (and_3_out, ~Curr[3], Curr[2], ~Curr[1]);  // AND_Gate
  and and_4 (and_4_out, ~Curr[3], Curr[2], ~Curr[0]);  // AND_Gate
  and and_5 (and_5_out, Curr[3], L);
  and and_6 (and_6_out, Curr[3], Z);
  and and_7 (and_7_out, ~Curr[3], ~Curr[1], Curr[0]);  // AND_Gate
  or or_1 (Next[1], and_7_out, and_8_out);
  and and_8 (and_8_out, ~Curr[3], Curr[1], ~Curr[0]);  // AND_Gate
  and and_9 (and_9_out, ~Curr[3], ~Curr[0], ~Z);  // AND_Gate
  and and_10 (and_10_out, ~Curr[3], Curr[1], ~Curr[0]);  // AND_Gate
  or or_2 (Next[0], and_9_out, and_10_out, and_11_out);
  and and_11 (and_11_out, ~Curr[3], Curr[2], ~Curr[0]);  // AND_Gate
  or or_3 (Next[2], and_2_out, and_3_out, and_4_out, and_5_out, and_6_out);
endmodule

module newton_test (
  output [7:0] Cycle,
  output [3:0] CurState,
  output [31:0] A,
  output [31:0] B,
  output [31:0] C,
  output [31:0] USERINPUT,
  output [31:0] D,
  output [31:0] RESULT,
  output [1:0] R,
  output [1:0] P,
  output [1:0] Q,
  output [2:0] Op,
  output L,
  output Z,
  output G,
  output [3:0] NextState,
  output halt
);

  wire and_1_out, and_2_out, clock_3_out, comparator_1_eq, comparator_3_eq, comparator_4_gt, counter_1_carry,
       decoder_1_out0, decoder_1_out1, decoder_1_out2, decoder_1_out3, funny, shift_register_1_p2,
       shift_register_1_p6;
  wire [1:0] comparator_5_gt;
  wire [3:0] shift_register_1_p3, shift_register_1_p4, shift_register_1_p5;
  wire [31:0] calc_alu_1_r, multiplexer_1_out, multiplexer_2_out;

  Clock clock_1 (.out(funny));
  Register #(.width(4)) register_1 (.D(NextState), .Q(CurState), .clk(funny));  // open: en, clr
  // Shift_Register #(.length(3), .width(4)) shift_register_1: pin names not known; wires that end beside it: CurState, shift_register_1_p2, shift_register_1_p3, shift_register_1_p4, shift_register_1_p5, shift_register_1_p6
  Clock clock_2 (.out(shift_register_1_p2));
  Decoder #(.enable("false"), .select(2)) decoder_1 (
    .out0(decoder_1_out0), .out1(decoder_1_out1), .out2(decoder_1_out2), .out3(decoder_1_out3), .sel(R));
  Comparator #(.width(4)) comparator_1 (.a(shift_register_1_p5), .b(CurState), .eq(comparator_1_eq));  // open: gt, lt
  Comparator #(.width(4)) comparator_2 (
    .a(shift_register_1_p4), .b(CurState), .eq(shift_register_1_p6));  // open: gt, lt
  Comparator #(.width(4)) comparator_3 (.a(shift_register_1_p3), .b(CurState), .eq(comparator_3_eq));  // open: gt, lt
  Register #(.width(32)) u_A (.D(RESULT), .en(decoder_1_out0), .Q(A), .clk(funny));  // open: clr
  Register #(.width(32)) u_B (.D(RESULT), .en(decoder_1_out1), .Q(B), .clk(funny));  // open: clr
  Register #(.width(32)) u_C (.D(RESULT), .en(decoder_1_out2), .Q(C), .clk(funny));  // open: clr
  Register #(.width(32)) u_D (.D(RESULT), .en(decoder_1_out3), .Q(D), .clk(funny));  // open: clr
  Clock clock_3 (.out(clock_3_out));
  Comparator #(.mode("unsigned")) comparator_4 (.a(Cycle), .b(8'hc), .gt(comparator_4_gt));  // open: eq, lt
  newton_output_table newton_output_table_1 (.Curr(CurState), .r(R), .p(P), .q(Q), .op(Op));
  Counter counter_1 (.Q(Cycle), .carry(counter_1_carry), .clk(clock_3_out));  // open: load, D, count, clr
  and and_1 (and_1_out, comparator_4_gt, comparator_1_eq, comparator_3_eq);
  Multiplexer #(.enable("false"), .select(2), .width(32)) multiplexer_1 (
    .in0(A), .in1(B), .in2(C), .in3(D), .out(multiplexer_1_out), .sel(P));
  Multiplexer #(.enable("false"), .select(2), .width(32)) multiplexer_2 (
    .in0(A), .in1(B), .in2(C), .in3(D), .out(multiplexer_2_out), .sel(Q));
  or or_1 (halt, counter_1_carry, and_1_out);
  calc_alu calc_alu_1 (.R(calc_alu_1_r), .P(multiplexer_1_out), .Q(multiplexer_2_out), .FN(Op));
  and and_2 (and_2_out, Op[0], Op[1], Op[2]);
  Comparator #(.mode("unsigned")) comparator_5 (.a(Cycle), .b(8'h3), .gt(comparator_5_gt[0]));  // open: eq, lt
  Comparator #(.mode("unsigned")) comparator_6 (.a(Cycle), .b(8'h40), .gt(comparator_5_gt[1]));  // open: eq, lt
  Multiplexer #(.enable("false"), .width(32)) multiplexer_3 (
    .in0(calc_alu_1_r), .in1(USERINPUT), .out(RESULT), .sel(and_2_out));
  Multiplexer #(.enable("false"), .select(2), .width(32)) multiplexer_4 (
    .in0({32{1'b1}}), .in1(32'h10), .in3(32'ha9), .out(USERINPUT), .sel(comparator_5_gt));  // open: in2
  calc_cmp calc_cmp_1 (.pos(G), .neg(L), .zero(Z), .V(RESULT));
  newton_transition_table newton_transition_table_1 (.Curr(CurState), .Z(Z), .L(L), .Next(NextState));

  // Notes on the sheet:
  //   r
  //   p
  //   Your state machine outputs should
  //   be connected here.
  //   q
  //   Your state machine goes here
  //   op
  //   L
  //   Z
  //   These are the
  //   inputs to your state machine
endmodule

module hailstone_test (
  output [7:0] Cycle,
  output [3:0] CurState,
  output [31:0] A,
  output [31:0] B,
  output [31:0] C,
  output [31:0] USERINPUT,
  output [31:0] D,
  output [31:0] RESULT,
  output [1:0] R,
  output [1:0] P,
  output [1:0] Q,
  output [2:0] Op,
  output L,
  output Z,
  output G,
  output [3:0] NextState,
  output halt
);

  wire and_1_out, and_2_out, clock_3_out, comparator_1_eq, comparator_3_eq, comparator_4_gt, counter_1_carry,
       decoder_1_out0, decoder_1_out1, decoder_1_out2, decoder_1_out3, rockfella, shift_register_1_p2,
       shift_register_1_p6;
  wire [3:0] shift_register_1_p3, shift_register_1_p4, shift_register_1_p5;
  wire [31:0] calc_alu_1_r, multiplexer_1_out, multiplexer_2_out;

  Clock clock_1 (.out(rockfella));
  Register #(.width(4)) register_1 (.D(NextState), .Q(CurState), .clk(rockfella));  // open: en, clr
  // Shift_Register #(.length(3), .width(4)) shift_register_1: pin names not known; wires that end beside it: CurState, shift_register_1_p2, shift_register_1_p3, shift_register_1_p4, shift_register_1_p5, shift_register_1_p6
  Clock clock_2 (.out(shift_register_1_p2));
  Decoder #(.enable("false"), .select(2)) decoder_1 (
    .out0(decoder_1_out0), .out1(decoder_1_out1), .out2(decoder_1_out2), .out3(decoder_1_out3), .sel(R));
  Comparator #(.width(4)) comparator_1 (.a(shift_register_1_p5), .b(CurState), .eq(comparator_1_eq));  // open: gt, lt
  Comparator #(.width(4)) comparator_2 (
    .a(shift_register_1_p4), .b(CurState), .eq(shift_register_1_p6));  // open: gt, lt
  Comparator #(.width(4)) comparator_3 (.a(shift_register_1_p3), .b(CurState), .eq(comparator_3_eq));  // open: gt, lt
  Register #(.width(32)) u_A (.D(RESULT), .en(decoder_1_out0), .Q(A), .clk(rockfella));  // open: clr
  Register #(.width(32)) u_B (.D(RESULT), .en(decoder_1_out1), .Q(B), .clk(rockfella));  // open: clr
  Register #(.width(32)) u_C (.D(RESULT), .en(decoder_1_out2), .Q(C), .clk(rockfella));  // open: clr
  Register #(.width(32)) u_D (.D(RESULT), .en(decoder_1_out3), .Q(D), .clk(rockfella));  // open: clr
  hailstone_output_table hailstone_output_table_1 (.curr(CurState), .r(R), .p(P), .q(Q), .op(Op));
  ROM #(.dataWidth(32)) rom_1 (.addr(Cycle), .data(USERINPUT));
  Counter counter_1 (.Q(Cycle), .carry(counter_1_carry), .clk(clock_3_out));  // open: load, D, count, clr
  Clock clock_3 (.out(clock_3_out));
  Comparator comparator_4 (.a(Cycle), .b(8'hc), .gt(comparator_4_gt));  // open: eq, lt
  and and_1 (and_1_out, comparator_4_gt, comparator_1_eq, comparator_3_eq);
  Multiplexer #(.enable("false"), .select(2), .width(32)) multiplexer_1 (
    .in0(A), .in1(B), .in2(C), .in3(D), .out(multiplexer_1_out), .sel(P));
  Multiplexer #(.enable("false"), .select(2), .width(32)) multiplexer_2 (
    .in0(A), .in1(B), .in2(C), .in3(D), .out(multiplexer_2_out), .sel(Q));
  or or_1 (halt, counter_1_carry, and_1_out);
  calc_alu calc_alu_1 (.R(calc_alu_1_r), .P(multiplexer_1_out), .Q(multiplexer_2_out), .FN(Op));
  and and_2 (and_2_out, Op[0], Op[1], Op[2]);
  Multiplexer #(.enable("false"), .width(32)) multiplexer_3 (
    .in0(calc_alu_1_r), .in1(USERINPUT), .out(RESULT), .sel(and_2_out));
  calc_cmp calc_cmp_1 (.pos(G), .neg(L), .zero(Z), .V(RESULT));
  hailstone_transition_table hailstone_transition_table_1 (.Curr(CurState), .Z(Z), .L(L), .Next(NextState));

  // Notes on the sheet:
  //   r
  //   r
  //   p
  //   Your state machine outputs should
  //   be connected here.
  //   contents of rom_1 (hex, n*v repeats v):
  //   0 0 0 c 24*0 c
  //   q
  //   Your state machine goes here
  //   op
  //   L
  //   Z
  //   These are the
  //   inputs to your state machine
endmodule
