// Logisim project sequential-test.circ as structural Verilog: 4 circuits, main circuit prng_test
module prng_test (
  output [4:0] cycle,
  output [15:0] seed,
  output reseed,
  output update,
  output [15:0] \rand ,
  output [15:0] expected,
  output ok,
  output halt
);

  wire clock_1_out, prng_1_p1;

  Counter #(.max('h1f), .width(5)) counter_1 (.Q(cycle), .carry(halt), .clk(clock_1_out));  // open: load, D, count, clr
  Clock clock_1 (.out(clock_1_out));
  ROM #(.addrWidth(5), .dataWidth(18)) rom_1 (.addr(cycle), .data({update, reseed, seed}));
  // prng prng_1: pin names not known; wires that end beside it: prng_1_p1, seed, reseed, update, prng_1_p1, \rand 
  prng_soln prng_soln_1 (.\rand (expected), .seed(seed), .reseed(reseed), .update(update));
  Comparator #(.width(16)) comparator_1 (.a(\rand ), .b(expected), .eq(ok));  // open: gt, lt

  // Notes on the sheet:
  //   contents of rom_1 (hex, n*v repeats v):
  //   0 0 11234 0 0 20000 0 20000 20000 20000 ffff 27777 0 0 1abcd 20000 20000 20000 0 0 3cafe 20000 20000
  //   20000 0 0 11234 4*20000
endmodule

module prng_soln (
  input  [15:0] seed,
  input  reseed,
  input  update,
  output [15:0] \rand 
);

  wire clock_1_out, not_1_out, or_1_out;
  wire [7:0] multiplier_1_out_2;
  wire [15:0] multiplexer_1_out, multiplier_1_out;
  wire [15:8] multiplier_1_cout;

  not not_1 (not_1_out, reseed);
  or or_1 (or_1_out, update, reseed);
  Multiplexer #(.enable("false"), .width(16)) multiplexer_1 (
    .in0(seed), .in1(multiplier_1_out), .out(multiplexer_1_out), .sel(not_1_out));
  Register #(.width(16)) register_1 (.D(multiplexer_1_out), .en(or_1_out), .Q(\rand ), .clk(clock_1_out));  // open: clr
  Clock clock_1 (.out(clock_1_out));
  Multiplier #(.width(16)) multiplier_1 (
    .a(\rand ), .b(\rand ), .out({multiplier_1_out[7:0], multiplier_1_out_2}),
    .cout({multiplier_1_cout, multiplier_1_out[15:8]}));  // open: cin
endmodule

module primefinder_test (
  output [6:0] cycle,
  output [31:0] StartingNumber,
  output [31:0] PrimeNumber,
  output done,
  output [31:0] Candidate,
  output [31:0] Register_i,
  output halt
);

  wire clock_1_out, clock_2_out, comparator_1_eq, not_1_out;
  wire [31:0] PrevInput_q;

  Counter #(.max('h7f), .width(7)) counter_1 (.Q(cycle), .carry(halt), .clk(clock_1_out));  // open: load, D, count, clr
  Clock clock_1 (.out(clock_1_out));
  ROM #(.addrWidth(7), .dataWidth(32)) rom_1 (.addr(cycle), .data(StartingNumber));
  Clock clock_2 (.out(clock_2_out));
  Register #(.width(32)) PrevInput (.D(StartingNumber), .Q(PrevInput_q), .clk(clock_2_out));  // open: en, clr
  not not_1 (not_1_out, comparator_1_eq);
  Comparator #(.width(32)) comparator_1 (.a(StartingNumber), .b(PrevInput_q), .eq(comparator_1_eq));  // open: gt, lt
  primefinder primefinder_1 (
    .StartingNumber(StartingNumber), .PrimeNumber(PrimeNumber), .done(done), .C(Candidate), .i(Register_i));

  // Notes on the sheet:
  //   contents of rom_1 (hex, n*v repeats v):
  //   0 21*18 10*4 48*20 2018 18 2018 18 2018 18 10*6
endmodule

module primefinder_soln (
  input  [31:0] StartingNumber,
  output [31:0] PrimeNumber,
  output out_3
);

  wire Clk, comparator_1_eq, comparator_3_eq, NewCand, NextCand, not_2_out, or_1_out, or_2_out, or_3_out;
  wire [31:0] adder_2_out, Cand_plus_1, divider_1_rem, i_q, multiplexer_1_out, multiplexer_2_out, PrevInput_q;

  Clock clock_1 (.out(Clk));
  Register #(.width(32)) PrevInput (.D(StartingNumber), .Q(PrevInput_q), .clk(Clk));  // open: en, clr
  not not_1 (NewCand, comparator_1_eq);
  Comparator #(.width(32)) comparator_1 (.a(StartingNumber), .b(PrevInput_q), .eq(comparator_1_eq));  // open: gt, lt
  Multiplexer #(.enable("false"), .width(32)) multiplexer_1 (
    .in0(Cand_plus_1), .in1(StartingNumber), .out(multiplexer_1_out), .sel(NewCand));
  or or_1 (or_1_out, NewCand, NextCand);
  or or_2 (or_2_out, NewCand, NextCand);
  not not_2 (not_2_out, or_2_out);
  Register #(.width(32)) Cand (.D(multiplexer_1_out), .en(or_1_out), .Q(PrimeNumber), .clk(Clk));  // open: clr
  Multiplexer #(.enable("false"), .width(32)) multiplexer_2 (
    .in0(32'h2), .in1(adder_2_out), .out(multiplexer_2_out), .sel(not_2_out));
  or or_3 (or_3_out, ~out_3, NewCand);  // OR_Gate
  Register #(.width(32)) i (.D(multiplexer_2_out), .en(or_3_out), .Q(i_q), .clk(Clk));  // open: clr
  Adder #(.width(32)) adder_1 (.a(PrimeNumber), .b(32'h1), .out(Cand_plus_1));  // open: cin, cout
  Comparator #(.width(32)) comparator_2 (.a(PrimeNumber), .b(i_q), .eq(out_3));  // open: gt, lt
  Divider #(.width(32)) divider_1 (.a(PrimeNumber), .b(i_q), .rem(divider_1_rem));  // open: out, upper
  Adder #(.width(32)) adder_2 (.a(i_q), .b(32'h1), .out(adder_2_out));  // open: cin, cout
  Comparator #(.width(32)) comparator_3 (.a(divider_1_rem), .b({32{1'b0}}), .eq(comparator_3_eq));  // open: gt, lt
  and and_1 (NextCand, ~out_3, comparator_3_eq);  // AND_Gate
  LED Done (.in(out_3));

  // Other names for the same wires on the sheet: Done = out_3

  // Notes on the sheet:
  //   Cand == i ?
  //   (Cand%i) == 0 ?
  //   Increment Candidate 
endmodule
